# Fritzing sketch sponge_test_stand__01 (saved by Fritzing 0.8.7b)
breadboards: 1

parts:
  Part1 = Arduino Uno (Rev3)  # not connected
  MD09B1 = A4988 Stepper Motor Driver Carrier  # not connected
  MD09B2 = A4988 Stepper Motor Driver Carrier  # not connected
  M2 = Stepper Motor - Unipolar  # not connected
  20V_3_25A = Power plug
  M3 = Stepper Motor - Unipolar  # not connected
  C4 = Electrolytic Capacitor [capacitance=100μF package="0807 [SMD, electrolytic]"]
  C5 = Electrolytic Capacitor [capacitance=100μF package="0807 [SMD, electrolytic]"]
  MD09B3 = A4988 Stepper Motor Driver Carrier  # not connected
  MD09B4 = A4988 Stepper Motor Driver Carrier  # not connected
  M4 = Stepper Motor - Unipolar  # not connected
  M5 = Stepper Motor - Unipolar  # not connected
  C6 = Electrolytic Capacitor [capacitance=100μF package="0807 [SMD, electrolytic]"]
  C7 = Electrolytic Capacitor [capacitance=100μF package="0807 [SMD, electrolytic]"]  # not connected

nets:
  N1: 20V_3_25A.GND, C4.-, C5.-, C6.-
  N2: 20V_3_25A.VCC, C4.+, C5.+, C6.+

notes:
  100µF, 16V
